# Fritzing sketch tank (saved by Fritzing 0.9.6b)
circuit board: 6.83359cm x 3.72446cm
breadboards: 1

parts:
  HC-SR04_Sensor_1 = HC-SR04 Ultrasonic Distance Sensor
  S2 = Taiway 100-SP-X-T1 SPDT Miniature Toggle Switch [part_number=100-SP-X-T1-0-0-B1-M1 package=THT]
  LED1 = LED - 5mm [color="Red (633nm)" current=0.030 package="5 mm [THT]"]
  S3 = Round Pushbutton
  M1 = DC Motor
  M2 = DC Motor
  VCC2 = Battery block 9V
  Part1 = DC-DC Power Module (5v)
  L298N1 = L298N DC motor driver
  220 = Resistor [tolerance=±5% resistance=220 power=0.25 package=THT]
  220_2 = Resistor [tolerance=±5% resistance=220 power=0.25 package=THT]
  220_3 = Resistor [tolerance=±5% resistance=220 power=0.25 package=THT]
  470 = Resistor [tolerance=±5% resistance=470 power=0.25 package=THT]
  MCU1 = Raspberry Pi Zero

nets:
  N1: HC-SR04_Sensor_1.VCC, Part1.Vout, MCU1.pin_2, MCU1.pin_4
  N2: HC-SR04_Sensor_1.TRIG, MCU1.pin_35
  N3: HC-SR04_Sensor_1.ECHO, 220_3.Pin_0
  N4: HC-SR04_Sensor_1.GND, Part1.GND*, 220.Pin_1, 220_2.Pin_1, 470.Pin_1, MCU1.pin_6, MCU1.pin_9, MCU1.pin_39
  VIN: S2.COM, Part1.Vin, L298N1.12V
  N5: S2.L2, VCC2.+
  N6: LED1.cathode, 220_2.Pin_0
  N7: LED1.anode, MCU1.pin_5
  N8: S3.leg0, MCU1.pin_7
  N9: S3.leg1, 220.Pin_0
  N10: M1.pin_1, L298N1.OUT2
  N11: M1.pin_2, L298N1.OUT1
  N12: M2.pin_1, L298N1.OUT4
  N13: M2.pin_2, L298N1.OUT3
  GND: VCC2.-, Part1.GND, L298N1.GND
  N14: L298N1.ENA, MCU1.pin_22
  N15: L298N1.ENB, MCU1.pin_19
  N16: L298N1.IN1, MCU1.pin_18
  N17: L298N1.IN2, MCU1.pin_16
  N18: L298N1.IN3, MCU1.pin_23
  N19: L298N1.IN4, MCU1.pin_21
  N20: 220_3.Pin_1, 470.Pin_0, MCU1.pin_37

notes:
  Actually an UBEC 3A 2-6S. 12-24v in, nice flat 5v out. I use 8 AA batteries as a power source.

custom parts:
  DC-DC Power Module (5v): DC-DC Power Module based con AMS1117-5.0 Input: DC 6~12V (input power must higher 1V than output power); Output: 5V (+/-0.05V error), 800mA
  L298N DC motor driver: 2x DC motor driver with 78M05 positive voltage regulator (7..35 V) L298N: max 46 V, 2 A Set 5 V Enable jumper to enable 5 V regultor (needed for the L298N) and +5 V output at screw terminal or supply external +5 V at screw terminal Set ENA and/or ENB to +5 V to enable motor permanently or supply ENA and/or ENB with PWM signal IN1 and IN2 set rotation directory for motor A (OUT1/OUT2) IN2 and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
