# Fritzing sketch tank_pcb (saved by Fritzing 0.9.6b)
circuit board: 6.83359cm x 3.72446cm
breadboards: 1

parts:
  +12v/gnd = male pin header, 2 pins [form="♂ (male)"]
  On/Off = male pin header, 2 pins [form="♂ (male)"]
  LED/Button = male pin header, 4 pins [form="♂ (male)"]
  DC/DC_conv = male pin header, 4 pins [form="♂ (male)"]
  HC-SR04 = male pin header, 4 pins [form="♂ (male)"]
  L298N = male pin header, 2 pins [form="♂ (male)"]
  220 = Resistor [tolerance=±5% resistance=220 power=0.25 package=THT]
  330 = Resistor [tolerance=±5% resistance=330 power=0.25 package=THT]
  330_2 = Resistor [tolerance=±5% resistance=330 power=0.25 package=THT]
  470 = Resistor [tolerance=±5% resistance=470 power=0.25 package=THT]
  MCU1 = Raspberry Pi Zero

nets:
  N1: +12v/gnd.pin1, DC/DC_conv.pin2, L298N.pin1
  N2: +12v/gnd.pin2, On/Off.pin1
  N3: On/Off.pin2, DC/DC_conv.pin1, L298N.pin2
  N4: LED/Button.pin1, 330.Pin_0
  N5: LED/Button.pin2, MCU1.pin_5
  N6: LED/Button.pin3, MCU1.pin_7
  N7: LED/Button.pin4, 220.Pin_0
  N8: DC/DC_conv.pin3, HC-SR04.pin4, 220.Pin_1, 330.Pin_1, 470.Pin_1, MCU1.pin_6, MCU1.pin_9, MCU1.pin_25, MCU1.pin_39
  N9: DC/DC_conv.pin4, HC-SR04.pin1, MCU1.pin_2
  N10: HC-SR04.pin2, MCU1.pin_35
  N11: HC-SR04.pin3, 330_2.Pin_0
  N12: 330_2.Pin_1, 470.Pin_0, MCU1.pin_37
